# Fritzing sketch BlinkToggle (saved by Fritzing 0.8.7b)
breadboards: 1

parts:
  Arduino_Uno_R3 = Arduino Uno (Rev3)
  R1 = Resistor [tolerance=±5% resistance=1k package=THT]
  LED1 = LED - 5mm [color="Red (633nm)" package="5 mm [THT]"]
  S1 = Toggle Switch [package=THT]
  Q1 = NPN-Transistor [package="TO92 [THT]"]
  R2 = Resistor [tolerance=±5% resistance=100 package=THT]

nets:
  N1: Arduino_Uno_R3.D2, S1.COM
  N2: Arduino_Uno_R3.D7, R1.Pin_0
  N3: Arduino_Uno_R3.5V, S1.L1, Q1.C
  GND: Arduino_Uno_R3.GND, LED1.cathode, S1.L2
  N4: R1.Pin_1, Q1.B
  N5: LED1.anode, R2.Pin_1
  N6: Q1.E, R2.Pin_0
